# Fritzing sketch NodeMCU_TMP102 (saved by Fritzing 0.9.3b)
breadboards: 1

parts:
  U1 = NodeMCU V1.0
  YwRobot_Power_Supply1 = YwRobot Breadboard Power Supply [part_number=545043]
  Part1 = Digital Temperature Sensor Breakout - TMP102

nets:
  N1: U1.D1, Part1.SDA
  N2: U1.D2, Part1.SCL
  N3: U1.3V3, Part1.V+
  GND: U1.GND, Part1.GND
  N4: YwRobot_Power_Supply1.GND#12, YwRobot_Power_Supply1.GND#14

custom parts:
  NodeMCU V1.0: ESP8266 based NodeMCU
  YwRobot Breadboard Power Supply: The YwRobot Breadboard Power Supply (MB-V2) has two power rails; they can be 5V or 3V3. Power to the module can be provided through the female USB socket or through the A10 (female) 2.1mm power jack.
